// Logisim project trabalho1_circuitos_versao_final.circ as structural Verilog: 10 circuits, main circuit operacao_and
module main (
  input  [15:0] A,
  input  [15:0] B,
  input  [2:0] Seletor,
  output [15:0] R,
  output Z
);

  mux mux_1 (.in_3(Seletor), .A(A), .B(B), .out_4(R), .Z(Z));
endmodule

module operacao_and (
  input  A16,
  input  A15,
  input  A14,
  input  A13,
  input  A12,
  input  A11,
  input  A10,
  input  A9,
  input  A8,
  input  A7,
  input  A6,
  input  A5,
  input  A4,
  input  A3,
  input  A2,
  input  A1,
  input  B16,
  input  B15,
  input  B14,
  input  B13,
  input  B12,
  input  B11,
  input  B10,
  input  B9,
  input  B8,
  input  B7,
  input  B6,
  input  B5,
  input  B4,
  input  B3,
  input  B2,
  input  B1,
  output R16,
  output R15,
  output R14,
  output R13,
  output R12,
  output R11,
  output R10,
  output R9,
  output R8,
  output R7,
  output R6,
  output R5,
  output R4,
  output R3,
  output R2,
  output R1
);

  and and_1 (R16, A16, B16);
  and and_2 (R15, A15, B15);
  and and_3 (R14, A14, B14);
  and and_4 (R13, A13, B13);
  and and_5 (R12, A12, B12);
  and and_6 (R11, A11, B11);
  and and_7 (R10, A10, B10);
  and and_8 (R9, A9, B9);
  and and_9 (R8, A8, B8);
  and and_10 (R7, A7, B7);
  and and_11 (R6, A6, B6);
  and and_12 (R5, A5, B5);
  and and_13 (R4, A4, B4);
  and and_14 (R3, A3, B3);
  and and_15 (R2, A2, B2);
  and and_16 (R1, A1, B1);
endmodule

module operacao_or (
  input  A16,
  input  A15,
  input  A14,
  input  A13,
  input  A12,
  input  A11,
  input  A10,
  input  A9,
  input  A8,
  input  A7,
  input  A6,
  input  A5,
  input  A4,
  input  A3,
  input  A2,
  input  A1,
  input  B16,
  input  B15,
  input  B14,
  input  B13,
  input  B12,
  input  B11,
  input  B10,
  input  B9,
  input  B8,
  input  B7,
  input  B6,
  input  B5,
  input  B4,
  input  B3,
  input  B2,
  input  B1,
  output R16,
  output R15,
  output R14,
  output R13,
  output R12,
  output R11,
  output R10,
  output R9,
  output R8,
  output R7,
  output R6,
  output R5,
  output R4,
  output R3,
  output R2,
  output R1
);

  or or_1 (R16, A16, B16);
  or or_2 (R15, A15, B15);
  or or_3 (R14, A14, B14);
  or or_4 (R13, A13, B13);
  or or_5 (R12, A12, B12);
  or or_6 (R11, A11, B11);
  or or_7 (R10, A10, B10);
  or or_8 (R9, A9, B9);
  or or_9 (R8, A8, B8);
  or or_10 (R7, A7, B7);
  or or_11 (R6, A6, B6);
  or or_12 (R5, A5, B5);
  or or_13 (R4, A4, B4);
  or or_14 (R3, A3, B3);
  or or_15 (R2, A2, B2);
  or or_16 (R1, A1, B1);
endmodule

module operacao_sub (
  input  A16,
  input  A15,
  input  A14,
  input  A13,
  input  A12,
  input  A11,
  input  A10,
  input  A9,
  input  A8,
  input  A7,
  input  A6,
  input  A5,
  input  A4,
  input  A3,
  input  A2,
  input  A1,
  input  B16,
  input  B15,
  input  B14,
  input  B13,
  input  B12,
  input  B11,
  input  B10,
  input  B9,
  input  B8,
  input  B7,
  input  B6,
  input  B5,
  input  B4,
  input  B3,
  input  B2,
  input  B1,
  input  Cin,
  output R16,
  output R15,
  output R14,
  output R13,
  output R12,
  output R11,
  output R10,
  output R9,
  output R8,
  output R7,
  output R6,
  output R5,
  output R4,
  output R3,
  output R2,
  output R1
);

  wire operacao_not_1_r1, operacao_not_1_r2, operacao_not_1_r3, operacao_not_1_r4, operacao_not_1_r5,
       operacao_not_1_r6, operacao_not_1_r7, operacao_not_1_r8, operacao_not_1_r9, operacao_not_1_r10,
       operacao_not_1_r11, operacao_not_1_r12, operacao_not_1_r13, operacao_not_1_r14, operacao_not_1_r15,
       operacao_not_1_r16;

  operacao_not operacao_not_1 (
    .A15(B15), .A14(B14), .A13(B13), .A12(B12), .A11(B11), .A10(B10), .A9(B9), .A8(B8), .A7(B7), .A6(B6),
    .A5(B5), .A4(B4), .A3(B3), .A2(B2), .A1(B1), .A16(B16), .R15(operacao_not_1_r15),
    .R14(operacao_not_1_r14), .R13(operacao_not_1_r13), .R12(operacao_not_1_r12), .R11(operacao_not_1_r11),
    .R10(operacao_not_1_r10), .R9(operacao_not_1_r9), .R8(operacao_not_1_r8), .R7(operacao_not_1_r7),
    .R6(operacao_not_1_r6), .R5(operacao_not_1_r5), .R4(operacao_not_1_r4), .R3(operacao_not_1_r3),
    .R2(operacao_not_1_r2), .R1(operacao_not_1_r1), .R16(operacao_not_1_r16));
  operacao_add operacao_add_1 (
    .B15(A15), .A15(operacao_not_1_r15), .B14(A14), .A14(operacao_not_1_r14), .B13(A13),
    .A13(operacao_not_1_r13), .B12(A12), .A12(operacao_not_1_r12), .B11(A11), .A11(operacao_not_1_r11),
    .B10(A10), .A10(operacao_not_1_r10), .B9(A9), .A9(operacao_not_1_r9), .B8(A8), .A8(operacao_not_1_r8),
    .B7(A7), .A7(operacao_not_1_r7), .B6(A6), .A6(operacao_not_1_r6), .B5(A5), .A5(operacao_not_1_r5),
    .B4(A4), .A4(operacao_not_1_r4), .B3(A3), .A3(operacao_not_1_r3), .B2(A2), .A2(operacao_not_1_r2),
    .B1(A1), .A1(operacao_not_1_r1), .B16(A16), .A16(operacao_not_1_r16), .Cin(Cin), .R5(R5), .R6(R6),
    .R7(R7), .R8(R8), .R9(R9), .R10(R10), .R1(R1), .R11(R11), .R12(R12), .R13(R13), .R14(R14), .R15(R15),
    .R16(R16), .R2(R2), .R3(R3), .R4(R4));
endmodule

module operacao_not (
  input  A16,
  input  A15,
  input  A14,
  input  A13,
  input  A12,
  input  A11,
  input  A10,
  input  A9,
  input  A8,
  input  A7,
  input  A6,
  input  A5,
  input  A4,
  input  A3,
  input  A2,
  input  A1,
  output R16,
  output R15,
  output R14,
  output R13,
  output R12,
  output R11,
  output R10,
  output R9,
  output R8,
  output R7,
  output R6,
  output R5,
  output R4,
  output R3,
  output R2,
  output R1
);

  not not_1 (R16, A16);
  not not_2 (R15, A15);
  not not_3 (R14, A14);
  not not_4 (R13, A13);
  not not_5 (R12, A12);
  not not_6 (R11, A11);
  not not_7 (R10, A10);
  not not_8 (R9, A9);
  not not_9 (R8, A8);
  not not_10 (R7, A7);
  not not_11 (R6, A6);
  not not_12 (R5, A5);
  not not_13 (R4, A4);
  not not_14 (R3, A3);
  not not_15 (R2, A2);
  not not_16 (R1, A1);
endmodule

module operacao_add (
  input  A16,
  input  A15,
  input  A14,
  input  A13,
  input  A12,
  input  A11,
  input  A10,
  input  A9,
  input  A8,
  input  A7,
  input  A6,
  input  A5,
  input  A4,
  input  A3,
  input  A2,
  input  A1,
  input  Cin,
  input  B16,
  input  B15,
  input  B14,
  input  B13,
  input  B12,
  input  B11,
  input  B10,
  input  B9,
  input  B8,
  input  B7,
  input  B6,
  input  B5,
  input  B4,
  input  B3,
  input  B2,
  input  B1,
  output R1,
  output R2,
  output R3,
  output R4,
  output R5,
  output R6,
  output R7,
  output R8,
  output R9,
  output R10,
  output R11,
  output R12,
  output R13,
  output R14,
  output R15,
  output R16
);

  wire full_adder_1_cout, full_adder_2_cout, full_adder_3_cout, full_adder_4_cout, full_adder_5_cout,
       full_adder_6_cout, full_adder_7_cout, full_adder_8_cout, full_adder_9_cout, full_adder_10_cout,
       full_adder_11_cout, full_adder_12_cout, full_adder_13_cout, full_adder_14_cout, full_adder_15_cout;

  full_adder full_adder_1 (.A(A1), .B(B1), .Cin(Cin), .R(R1), .Cout(full_adder_1_cout));
  full_adder full_adder_2 (.A(A2), .B(B2), .Cin(full_adder_1_cout), .R(R2), .Cout(full_adder_2_cout));
  full_adder full_adder_3 (.A(A3), .B(B3), .Cin(full_adder_2_cout), .R(R3), .Cout(full_adder_3_cout));
  full_adder full_adder_4 (.A(A4), .B(B4), .Cin(full_adder_3_cout), .R(R4), .Cout(full_adder_4_cout));
  full_adder full_adder_5 (.A(A5), .B(B5), .Cin(full_adder_4_cout), .R(R5), .Cout(full_adder_5_cout));
  full_adder full_adder_6 (.A(A6), .B(B6), .Cin(full_adder_5_cout), .R(R6), .Cout(full_adder_6_cout));
  full_adder full_adder_7 (.A(A7), .B(B7), .Cin(full_adder_6_cout), .R(R7), .Cout(full_adder_7_cout));
  full_adder full_adder_8 (.A(A8), .B(B8), .Cin(full_adder_7_cout), .R(R8), .Cout(full_adder_8_cout));
  full_adder full_adder_9 (.A(A9), .B(B9), .Cin(full_adder_8_cout), .R(R9), .Cout(full_adder_9_cout));
  full_adder full_adder_10 (.A(A10), .B(B10), .Cin(full_adder_9_cout), .R(R10), .Cout(full_adder_10_cout));
  full_adder full_adder_11 (.A(A11), .B(B11), .Cin(full_adder_10_cout), .R(R11), .Cout(full_adder_11_cout));
  full_adder full_adder_12 (.A(A12), .B(B12), .Cin(full_adder_11_cout), .R(R12), .Cout(full_adder_12_cout));
  full_adder full_adder_13 (.A(A13), .B(B13), .Cin(full_adder_12_cout), .R(R13), .Cout(full_adder_13_cout));
  full_adder full_adder_14 (.A(A14), .B(B14), .Cin(full_adder_13_cout), .R(R14), .Cout(full_adder_14_cout));
  full_adder full_adder_15 (.A(A15), .B(B15), .Cin(full_adder_14_cout), .R(R15), .Cout(full_adder_15_cout));
  // full_adder full_adder_16: pin names not known; wires that end beside it: A16, B16, full_adder_15_cout, R16, 1'b0
endmodule

module full_adder (
  input  A,
  input  B,
  input  Cin,
  output R,
  output Cout
);

  wire and_1_out, and_2_out, and_3_out, or_1_out, xor_1_out;

  xor xor_1 (xor_1_out, A, B);
  and and_1 (and_1_out, A, B);
  and and_2 (and_2_out, Cin, A);
  and and_3 (and_3_out, B, Cin);
  xor xor_2 (R, xor_1_out, Cin);
  or or_1 (or_1_out, and_1_out, and_2_out);
  or or_2 (Cout, or_1_out, and_3_out);
endmodule

module operacao_eql (
  input  A16,
  input  A15,
  input  A14,
  input  A13,
  input  A12,
  input  A11,
  input  A10,
  input  A9,
  input  A8,
  input  A7,
  input  A6,
  input  A5,
  input  A4,
  input  A3,
  input  A2,
  input  A1,
  input  B16,
  input  B15,
  input  B14,
  input  B13,
  input  B12,
  input  B11,
  input  B10,
  input  B9,
  input  B8,
  input  B7,
  input  B6,
  input  B5,
  input  B4,
  input  B3,
  input  B2,
  input  B1,
  output R16,
  output R15,
  output R14,
  output R13,
  output R12,
  output R11,
  output R10,
  output R9,
  output R8,
  output R7,
  output R6,
  output R5,
  output R4,
  output R3,
  output R2,
  output R1
);

  wire and_1_out, and_2_out, and_3_out, and_4_out, and_5_out, and_6_out, and_7_out, and_8_out, and_9_out,
       and_10_out, and_11_out, and_12_out, and_13_out, and_14_out, xnor_1_out, xnor_2_out, xnor_3_out,
       xnor_4_out, xnor_5_out, xnor_6_out, xnor_7_out, xnor_8_out, xnor_9_out, xnor_10_out, xnor_11_out,
       xnor_12_out, xnor_13_out, xnor_14_out, xnor_15_out, xnor_16_out;

  xnor xnor_1 (xnor_1_out, A16, B16);
  xnor xnor_2 (xnor_2_out, A15, B15);
  xnor xnor_3 (xnor_3_out, A14, B14);
  xnor xnor_4 (xnor_4_out, A13, B13);
  xnor xnor_5 (xnor_5_out, A12, B12);
  xnor xnor_6 (xnor_6_out, A11, B11);
  xnor xnor_7 (xnor_7_out, A10, B10);
  xnor xnor_8 (xnor_8_out, A9, B9);
  xnor xnor_9 (xnor_9_out, A8, B8);
  xnor xnor_10 (xnor_10_out, A7, B7);
  xnor xnor_11 (xnor_11_out, A6, B6);
  xnor xnor_12 (xnor_12_out, A5, B5);
  xnor xnor_13 (xnor_13_out, A4, B4);
  xnor xnor_14 (xnor_14_out, A3, B3);
  xnor xnor_15 (xnor_15_out, A2, B2);
  xnor xnor_16 (xnor_16_out, A1, B1);
  and and_1 (and_1_out, xnor_1_out, xnor_2_out);
  and and_2 (and_2_out, xnor_3_out, xnor_4_out);
  and and_3 (and_3_out, xnor_5_out, xnor_6_out);
  and and_4 (and_4_out, xnor_7_out, xnor_8_out);
  and and_5 (and_5_out, xnor_9_out, xnor_10_out);
  and and_6 (and_6_out, xnor_11_out, xnor_12_out);
  and and_7 (and_7_out, xnor_13_out, xnor_14_out);
  and and_8 (and_8_out, xnor_15_out, xnor_16_out);
  and and_9 (and_9_out, and_1_out, and_2_out);
  and and_10 (and_10_out, and_3_out, and_4_out);
  and and_11 (and_11_out, and_5_out, and_6_out);
  and and_12 (and_12_out, and_7_out, and_8_out);
  and and_13 (and_13_out, and_9_out, and_10_out);
  and and_14 (and_14_out, and_11_out, and_12_out);
  and and_15 (R1, and_13_out, and_14_out);

  assign R2 = R1;
  assign R3 = R1;
  assign R4 = R1;
  assign R5 = R1;
  assign R6 = R1;
  assign R7 = R1;
  assign R8 = R1;
  assign R9 = R1;
  assign R10 = R1;
  assign R11 = R1;
  assign R12 = R1;
  assign R13 = R1;
  assign R14 = R1;
  assign R15 = R1;
  assign R16 = R1;
endmodule

module mux (
  input  [15:0] A,
  input  [15:0] B,
  input  [2:0] in_3,
  output [15:0] out_4,
  output Z
);

  wire [15:0] R1, R2, R3, R4, R5, R6;

  operacao_and operacao_and_1 (
    .B15(B[14]), .A15(A[14]), .B14(B[13]), .A14(A[13]), .B13(B[12]), .A13(A[12]), .B12(B[11]), .A12(A[11]),
    .B11(B[10]), .A11(A[10]), .B10(B[9]), .A10(A[9]), .B9(B[8]), .A9(A[8]), .B8(B[7]), .A8(A[7]), .B7(B[6]),
    .A7(A[6]), .B6(B[5]), .A6(A[5]), .B5(B[4]), .A5(A[4]), .B4(B[3]), .A4(A[3]), .B3(B[2]), .A3(A[2]),
    .B2(B[1]), .A2(A[1]), .B1(B[0]), .A1(A[0]), .B16(B[15]), .A16(A[15]), .R8(R1[7]), .R7(R1[6]), .R6(R1[5]),
    .R5(R1[4]), .R4(R1[3]), .R3(R1[2]), .R2(R1[1]), .R1(R1[0]), .R16(R1[15]), .R15(R1[14]), .R14(R1[13]),
    .R13(R1[12]), .R12(R1[11]), .R11(R1[10]), .R10(R1[9]), .R9(R1[8]));
  operacao_or operacao_or_1 (
    .B15(B[14]), .A15(A[14]), .B14(B[13]), .A14(A[13]), .B13(B[12]), .A13(A[12]), .B12(B[11]), .A12(A[11]),
    .B11(B[10]), .A11(A[10]), .B10(B[9]), .A10(A[9]), .B9(B[8]), .A9(A[8]), .B8(B[7]), .A8(A[7]), .B7(B[6]),
    .A7(A[6]), .B6(B[5]), .A6(A[5]), .B5(B[4]), .A5(A[4]), .B4(B[3]), .A4(A[3]), .B3(B[2]), .A3(A[2]),
    .B2(B[1]), .A2(A[1]), .B1(B[0]), .A1(A[0]), .B16(B[15]), .A16(A[15]), .R8(R2[7]), .R7(R2[6]), .R6(R2[5]),
    .R5(R2[4]), .R4(R2[3]), .R3(R2[2]), .R2(R2[1]), .R1(R2[0]), .R16(R2[15]), .R15(R2[14]), .R14(R2[13]),
    .R13(R2[12]), .R12(R2[11]), .R11(R2[10]), .R10(R2[9]), .R9(R2[8]));
  operacao_add operacao_add_1 (
    .B15(B[14]), .A15(A[14]), .B14(B[13]), .A14(A[13]), .B13(B[12]), .A13(A[12]), .B12(B[11]), .A12(A[11]),
    .B11(B[10]), .A11(A[10]), .B10(B[9]), .A10(A[9]), .B9(B[8]), .A9(A[8]), .B8(B[7]), .A8(A[7]), .B7(B[6]),
    .A7(A[6]), .B6(B[5]), .A6(A[5]), .B5(B[4]), .A5(A[4]), .B4(B[3]), .A4(A[3]), .B3(B[2]), .A3(A[2]),
    .B2(B[1]), .A2(A[1]), .B1(B[0]), .A1(A[0]), .B16(B[15]), .A16(A[15]), .Cin(1'b0), .R5(R6[4]), .R6(R6[5]),
    .R7(R6[6]), .R8(R6[7]), .R9(R6[8]), .R10(R6[9]), .R1(R6[0]), .R11(R6[10]), .R12(R6[11]), .R13(R6[12]),
    .R14(R6[13]), .R15(R6[14]), .R16(R6[15]), .R2(R6[1]), .R3(R6[2]), .R4(R6[3]));
  operacao_sub operacao_sub_1 (
    .B15(B[14]), .A15(A[14]), .B14(B[13]), .A14(A[13]), .B13(B[12]), .A13(A[12]), .B12(B[11]), .A12(A[11]),
    .B11(B[10]), .A11(A[10]), .B10(B[9]), .A10(A[9]), .B9(B[8]), .A9(A[8]), .B8(B[7]), .A8(A[7]), .B7(B[6]),
    .A7(A[6]), .B6(B[5]), .A6(A[5]), .Cin(1'b1), .B5(B[4]), .A5(A[4]), .B4(B[3]), .A4(A[3]), .B3(B[2]),
    .A3(A[2]), .B2(B[1]), .A2(A[1]), .B1(B[0]), .A1(A[0]), .B16(B[15]), .A16(A[15]), .R16(R3[15]),
    .R15(R3[14]), .R14(R3[13]), .R13(R3[12]), .R12(R3[11]), .R11(R3[10]), .R10(R3[9]), .R9(R3[8]),
    .R8(R3[7]), .R7(R3[6]), .R6(R3[5]), .R5(R3[4]), .R4(R3[3]), .R3(R3[2]), .R2(R3[1]), .R1(R3[0]));
  operacao_not operacao_not_1 (
    .A15(A[14]), .A14(A[13]), .A13(A[12]), .A12(A[11]), .A11(A[10]), .A10(A[9]), .A9(A[8]), .A8(A[7]),
    .A7(A[6]), .A6(A[5]), .A5(A[4]), .A4(A[3]), .A3(A[2]), .A2(A[1]), .A1(A[0]), .A16(A[15]), .R15(R4[14]),
    .R14(R4[13]), .R13(R4[12]), .R12(R4[11]), .R11(R4[10]), .R10(R4[9]), .R9(R4[8]), .R8(R4[7]), .R7(R4[6]),
    .R6(R4[5]), .R5(R4[4]), .R4(R4[3]), .R3(R4[2]), .R2(R4[1]), .R1(R4[0]), .R16(R4[15]));
  operacao_eql operacao_eql_1 (
    .B15(B[14]), .A15(A[14]), .B14(B[13]), .A14(A[13]), .B13(B[12]), .A13(A[12]), .B12(B[11]), .A12(A[11]),
    .B11(B[10]), .A11(A[10]), .B10(B[9]), .A10(A[9]), .B9(B[8]), .A9(A[8]), .B8(B[7]), .A8(A[7]), .B7(B[6]),
    .A7(A[6]), .B6(B[5]), .A6(A[5]), .B5(B[4]), .A5(A[4]), .B4(B[3]), .A4(A[3]), .B3(B[2]), .A3(A[2]),
    .B2(B[1]), .A2(A[1]), .B1(B[0]), .A1(A[0]), .B16(B[15]), .A16(A[15]), .R4(R5[3]), .R3(R5[2]), .R2(R5[1]),
    .R1(R5[0]), .R16(R5[15]), .R15(R5[14]), .R14(R5[13]), .R13(R5[12]), .R12(R5[11]), .R11(R5[10]),
    .R10(R5[9]), .R9(R5[8]), .R8(R5[7]), .R7(R5[6]), .R6(R5[5]), .R5(R5[4]));
  Multiplexer #(.select(3), .width(16)) multiplexer_1 (
    .in0(R1), .in1(R2), .in2(R3), .in3(R4), .in4(R5), .in5(R6), .in6({16{1'b0}}), .in7({16{1'b0}}),
    .out(out_4), .sel(in_3));
  detector_de_zero detector_de_zero_1 (
    .A15(out_4[14]), .A14(out_4[13]), .A13(out_4[12]), .A12(out_4[11]), .A11(out_4[10]), .A10(out_4[9]),
    .A9(out_4[8]), .A8(out_4[7]), .A7(out_4[6]), .A6(out_4[5]), .A5(out_4[4]), .A4(out_4[3]), .A3(out_4[2]),
    .A2(out_4[1]), .A1(out_4[0]), .A16(out_4[15]), .Z(Z));
endmodule

module detector_de_zero (
  input  A16,
  input  A15,
  input  A14,
  input  A13,
  input  A12,
  input  A11,
  input  A10,
  input  A9,
  input  A8,
  input  A7,
  input  A6,
  input  A5,
  input  A4,
  input  A3,
  input  A2,
  input  A1,
  output Z
);

  wire or_1_out, or_2_out, or_3_out, or_4_out, or_5_out, or_6_out, or_7_out, or_8_out, or_9_out, or_10_out,
       or_11_out, or_12_out, or_13_out, or_14_out;

  or or_1 (or_1_out, A16, A15);
  or or_2 (or_2_out, A14, A13);
  or or_3 (or_3_out, A12, A11);
  or or_4 (or_4_out, A10, A9);
  or or_5 (or_5_out, A8, A7);
  or or_6 (or_6_out, A6, A5);
  or or_7 (or_7_out, A4, A3);
  or or_8 (or_8_out, A2, A1);
  or or_9 (or_9_out, or_1_out, or_2_out);
  or or_10 (or_10_out, or_3_out, or_4_out);
  or or_11 (or_11_out, or_5_out, or_6_out);
  or or_12 (or_12_out, or_7_out, or_8_out);
  or or_13 (or_13_out, or_9_out, or_10_out);
  or or_14 (or_14_out, or_11_out, or_12_out);
  nor nor_1 (Z, or_13_out, or_14_out);
endmodule
