// Logisim project trabalho2_versãofinal.circ as structural Verilog: 3 circuits, main circuit main
module main (
);

  wire and_1_out, and_2_out, and_3_out, and_4_out, and_5_out, and_6_out, B, Botao_pedestre_out, clock_1_out,
       E0, E1, E2, not_1_out, not_2_out, not_3_out, not_4_out, not_5_out, not_6_out, not_7_out, not_8_out,
       or_1_out, or_2_out, semaforo_2_1_amarelo, semaforo_2_1_verde, semaforo_2_1_vermelho,
       semaforos_1_e_3_1_amarelo, semaforos_1_e_3_1_verde, semaforos_1_e_3_1_vermelho;

  Button Botao_pedestre (.out(Botao_pedestre_out));
  not not_1 (not_1_out, E2);
  not not_2 (not_2_out, E2);
  not not_3 (not_3_out, E1);
  not not_4 (not_4_out, B);
  not not_5 (not_5_out, E0);
  not not_6 (not_6_out, E0);
  not not_7 (not_7_out, E2);
  not not_8 (not_8_out, E0);
  and and_1 (and_1_out, not_1_out, E0, B);
  and and_2 (and_2_out, not_7_out, not_8_out);
  and and_3 (and_3_out, E1, B);
  S_R_Flip_Flop #(.trigger("high")) s_r_ff_1 (
    .S(Botao_pedestre_out), .R(E2), .clk(1'b1), .Q(B));  // open: reset, Qn, preset
  and and_4 (and_4_out, not_2_out, not_3_out, E0, not_4_out);
  and and_5 (and_5_out, not_5_out, E2);
  and and_6 (and_6_out, not_6_out, E1);
  or or_1 (or_1_out, and_2_out, and_3_out);
  or or_2 (or_2_out, and_4_out, and_5_out, and_6_out);
  Clock clock_1 (.out(clock_1_out));
  D_Flip_Flop d_ff_1 (.D(and_1_out), .clk(clock_1_out), .Q(E2));  // open: Qn, preset, reset
  D_Flip_Flop d_ff_2 (.D(or_2_out), .clk(clock_1_out), .Q(E1));  // open: Qn, preset, reset
  D_Flip_Flop d_ff_3 (.D(or_1_out), .clk(clock_1_out), .Q(E0));  // open: Qn, preset, reset
  LED Semaforos_pedestre (.in(E2));
  semaforos_1_e_3 semaforos_1_e_3_1 (
    .E0(E0), .E2(E2), .E1(E1), .vermelho(semaforos_1_e_3_1_vermelho), .amarelo(semaforos_1_e_3_1_amarelo),
    .verde(semaforos_1_e_3_1_verde));
  LED led_1 (.in(semaforo_2_1_vermelho));
  semaforo_2 semaforo_2_1 (
    .E1ff(E1), .E0ff(E0), .vermelho(semaforo_2_1_vermelho), .amarelo(semaforo_2_1_amarelo),
    .verde(semaforo_2_1_verde));
  LED led_2 (.in(semaforo_2_1_amarelo));
  LED led_3 (.in(semaforo_2_1_verde));
  LED led_4 (.in(semaforos_1_e_3_1_vermelho));
  LED led_5 (.in(semaforos_1_e_3_1_amarelo));
  LED led_6 (.in(semaforos_1_e_3_1_verde));

  // Other names for the same wires on the sheet: E0ff = E0; E1ff = E1; E2ff = E2
endmodule

module semaforos_1_e_3 (
  input  E0,
  input  E2,
  input  E1,
  output vermelho,
  output amarelo,
  output verde
);

  wire and_1_out, not_1_out, not_2_out, not_3_out, not_4_out, not_5_out, S0, S1;

  not not_1 (not_1_out, E2);
  not not_2 (not_2_out, E1);
  and and_1 (and_1_out, not_1_out, not_2_out);
  not not_3 (not_3_out, E0);
  and and_2 (S1, not_3_out, and_1_out);
  and and_3 (S0, and_1_out, E0);
  not not_4 (not_4_out, S1);
  not not_5 (not_5_out, S0);
  nor nor_1 (vermelho, S1, S0);
  and and_4 (amarelo, not_4_out, S0);
  and and_5 (verde, S1, not_5_out);
endmodule

module semaforo_2 (
  input  E1ff,
  input  E0ff,
  output vermelho,
  output amarelo,
  output verde
);

  wire not_1_out, not_2_out, not_3_out, S0, S1;

  not not_1 (not_1_out, E0ff);
  and u_S1 (S1, E1ff, not_1_out);
  and u_S0 (S0, E1ff, E0ff);
  not not_2 (not_2_out, S1);
  not not_3 (not_3_out, S0);
  nor nor_1 (vermelho, S1, S0);
  and and_1 (amarelo, not_2_out, S0);
  and and_2 (verde, S1, not_3_out);
endmodule
